// Logisim project cpu.circ as structural Verilog: 1 circuit, main circuit cpu
module cpu (
  input  clk,
  input  [31:0] Instruction,
  input  [31:0] MemReadData,
  output [31:0] MemAddress,
  output [31:0] ProgramCounter,
  output [31:0] ra,
  output [31:0] sp,
  output [31:0] t0,
  output [31:0] t1,
  output [31:0] t2,
  output [31:0] s0,
  output [31:0] s1,
  output [31:0] a0,
  output [3:0] MemWriteMask,
  output [31:0] MemWriteData
);

  wire control_logic_1_regwen, partial_store_1_p1, partial_store_1_p2, partial_store_1_p4, partial_store_1_p6;
  wire [2:0] control_logic_1_immsel;
  wire [3:0] control_logic_1_alusel;
  wire [31:0] adder_1_out, alu_1_aluresult, imm_gen_1_immediate, regfile_1_readdata1;

  Register #(.width(32)) PC (.D(adder_1_out), .clk(clk), .Q(ProgramCounter));  // open: en, clr
  Adder #(.width(32)) adder_1 (.a(ProgramCounter), .b(32'h4), .out(adder_1_out));  // open: cin, cout
  control_logic control_logic_1 (
    .Instruction(Instruction), .RegWEn(control_logic_1_regwen), .ImmSel(control_logic_1_immsel),
    .ALUSel(control_logic_1_alusel));  // open: BrEq, BrLt, PCSel, BrUn, ASel, BSel, MemWEn, WBSel
  regfile regfile_1 (
    .ReadIndex1(Instruction[19:15]), .WriteIndex(Instruction[11:7]), .WriteData(alu_1_aluresult),
    .RegWEn(control_logic_1_regwen), .clk(clk), .ra(ra), .sp(sp), .t0(t0), .t1(t1), .t2(t2), .s0(s0),
    .s1(s1), .a0(a0), .ReadData1(regfile_1_readdata1));  // open: ReadIndex2, ReadData2
  imm_gen imm_gen_1 (.Instruction(Instruction), .ImmSel(control_logic_1_immsel), .Immediate(imm_gen_1_immediate));
  alu alu_1 (
    .A(regfile_1_readdata1), .B(imm_gen_1_immediate), .ALUSel(control_logic_1_alusel),
    .ALUResult(alu_1_aluresult));
  // branch_comp branch_comp_1: pin names not known
  // partial_store partial_store_1: pin names not known; wires that end beside it: partial_store_1_p1, partial_store_1_p2, partial_store_1_p2, partial_store_1_p4, partial_store_1_p4, partial_store_1_p6, partial_store_1_p1, partial_store_1_p6
  // partial_load partial_load_1: pin names not known

  // Other names for the same wires on the sheet: opcode1[6:0] = Instruction[6:0]; rd1[4:0] = Instruction[11:7];
  //   funct3[2:0] = Instruction[14:12]; rs1[4:0] = Instruction[19:15]; imm[11:0] = Instruction[31:20]

  // Notes on the sheet:
  //   To IMEM
  //   IMEM (do **NOT** move this)
  //   From IMEM
  //   Inputs/Outputs for testing. Do **NOT** move these.
  //   It is OK to move the PC, RegFile, ALU, MEM, Branch Comp, Imm Gen, Partial Load, Partial Store and Control Logic to wherever is most convenient for you when constructing your CPU, and to delete this text
  //   To DMEM
  //   DMEM (do **NOT** move this)
  //   From DMEM
endmodule
