// Logisim project regfile.circ as structural Verilog: 1 circuit, main circuit regfile
module regfile (
  input  [4:0] ReadIndex1,
  input  [4:0] ReadIndex2,
  input  [4:0] WriteIndex,
  input  [31:0] WriteData,
  input  RegWEn,
  input  clk,
  output [31:0] ra,
  output [31:0] sp,
  output [31:0] t0,
  output [31:0] t1,
  output [31:0] t2,
  output [31:0] s0,
  output [31:0] s1,
  output [31:0] a0,
  output [31:0] ReadData1,
  output [31:0] ReadData2
);

  wire x1a, x2a, x3a, x4a, x5a, x6a, x7a, x8a, x9a, x10a, x11a, x12a, x13a, x14a, x15a, x16a, x17a, x18a,
       x19a, x20a, x21a, x22a, x23a, x24a, x25a, x26a, x27a, x28a, x29a, x30a, x31a;
  wire [31:0] x0, x3, x4, x11, x12, x13, x14, x15, x16, x17, x18, x19, x20, x21, x22, x23, x24, x25, x26,
       x27, x28, x29, x30, x31;

  Register #(.width(32)) register_1 (.D(WriteData), .en(1'b0), .clk(clk), .Q(x0), .clr(1'b0));
  Register #(.width(32)) register_2 (.D(WriteData), .en(x1a), .clk(clk), .Q(ra), .clr(1'b0));
  Register #(.width(32)) register_3 (.D(WriteData), .en(x2a), .clk(clk), .Q(sp), .clr(1'b0));
  Register #(.width(32)) register_4 (.D(WriteData), .en(x3a), .clk(clk), .Q(x3), .clr(1'b0));
  Register #(.width(32)) register_5 (.D(WriteData), .en(x4a), .clk(clk), .Q(x4), .clr(1'b0));
  Register #(.width(32)) register_6 (.D(WriteData), .en(x5a), .clk(clk), .Q(t0), .clr(1'b0));
  Register #(.width(32)) register_7 (.D(WriteData), .en(x6a), .clk(clk), .Q(t1), .clr(1'b0));
  Register #(.width(32)) register_8 (.D(WriteData), .en(x7a), .clk(clk), .Q(t2), .clr(1'b0));
  Register #(.width(32)) register_9 (.D(WriteData), .en(x8a), .clk(clk), .Q(s0), .clr(1'b0));
  Register #(.width(32)) register_10 (.D(WriteData), .en(x9a), .clk(clk), .Q(s1), .clr(1'b0));
  Register #(.width(32)) register_11 (.D(WriteData), .en(x10a), .clk(clk), .Q(a0), .clr(1'b0));
  Register #(.width(32)) register_12 (.D(WriteData), .en(x11a), .clk(clk), .Q(x11), .clr(1'b0));
  Register #(.width(32)) register_13 (.D(WriteData), .en(x12a), .clk(clk), .Q(x12), .clr(1'b0));
  Register #(.width(32)) register_14 (.D(WriteData), .en(x13a), .clk(clk), .Q(x13), .clr(1'b0));
  Register #(.width(32)) register_15 (.D(WriteData), .en(x14a), .clk(clk), .Q(x14), .clr(1'b0));
  Register #(.width(32)) register_16 (.D(WriteData), .en(x15a), .clk(clk), .Q(x15), .clr(1'b0));
  Register #(.width(32)) register_17 (.D(WriteData), .en(x16a), .clk(clk), .Q(x16), .clr(1'b0));
  Register #(.width(32)) register_18 (.D(WriteData), .en(x17a), .clk(clk), .Q(x17), .clr(1'b0));
  Register #(.width(32)) register_19 (.D(WriteData), .en(x18a), .clk(clk), .Q(x18), .clr(1'b0));
  Register #(.width(32)) register_20 (.D(WriteData), .en(x19a), .clk(clk), .Q(x19), .clr(1'b0));
  Register #(.width(32)) register_21 (.D(WriteData), .en(x20a), .clk(clk), .Q(x20), .clr(1'b0));
  Register #(.width(32)) register_22 (.D(WriteData), .en(x21a), .clk(clk), .Q(x21), .clr(1'b0));
  Register #(.width(32)) register_23 (.D(WriteData), .en(x22a), .clk(clk), .Q(x22), .clr(1'b0));
  Register #(.width(32)) register_24 (.D(WriteData), .en(x23a), .clk(clk), .Q(x23), .clr(1'b0));
  Register #(.width(32)) register_25 (.D(WriteData), .en(x24a), .clk(clk), .Q(x24), .clr(1'b0));
  Register #(.width(32)) register_26 (.D(WriteData), .en(x25a), .clk(clk), .Q(x25), .clr(1'b0));
  Register #(.width(32)) register_27 (.D(WriteData), .en(x26a), .clk(clk), .Q(x26), .clr(1'b0));
  Register #(.width(32)) register_28 (.D(WriteData), .en(x27a), .clk(clk), .Q(x27), .clr(1'b0));
  Register #(.width(32)) register_29 (.D(WriteData), .en(x28a), .clk(clk), .Q(x28), .clr(1'b0));
  Register #(.width(32)) register_30 (.D(WriteData), .en(x29a), .clk(clk), .Q(x29), .clr(1'b0));
  Register #(.width(32)) register_31 (.D(WriteData), .en(x30a), .clk(clk), .Q(x30), .clr(1'b0));
  Register #(.width(32)) register_32 (.D(WriteData), .en(x31a), .clk(clk), .Q(x31), .clr(1'b0));
  Demultiplexer #(.select(5)) demultiplexer_1 (
    .out1(x1a), .out2(x2a), .out3(x3a), .out4(x4a), .out5(x5a), .out6(x6a), .out7(x7a), .out8(x8a),
    .out9(x9a), .out10(x10a), .out11(x11a), .out12(x12a), .out13(x13a), .out14(x14a), .out15(x15a),
    .out16(x16a), .out17(x17a), .out18(x18a), .out19(x19a), .out20(x20a), .out21(x21a), .out22(x22a),
    .out23(x23a), .out24(x24a), .out25(x25a), .out26(x26a), .out27(x27a), .out28(x28a), .out29(x29a),
    .out30(x30a), .out31(x31a), .in(RegWEn), .sel(WriteIndex));  // open: out0
  Multiplexer #(.select(5), .width(32)) multiplexer_1 (
    .in0(x0), .in1(ra), .in2(sp), .in3(x3), .in4(x4), .in5(t0), .in6(t1), .in7(t2), .in8(s0), .in9(s1),
    .in10(a0), .in11(x11), .in12(x12), .in13(x13), .in14(x14), .in15(x15), .in16(x16), .in17(x17),
    .in18(x18), .in19(x19), .in20(x20), .in21(x21), .in22(x22), .in23(x23), .in24(x24), .in25(x25),
    .in26(x26), .in27(x27), .in28(x28), .in29(x29), .in30(x30), .in31(x31), .out(ReadData1), .sel(ReadIndex1));
  Multiplexer #(.select(5), .width(32)) multiplexer_2 (
    .in0(x0), .in1(ra), .in2(sp), .in3(x3), .in4(x4), .in5(t0), .in6(t1), .in7(t2), .in8(s0), .in9(s1),
    .in10(a0), .in11(x11), .in12(x12), .in13(x13), .in14(x14), .in15(x15), .in16(x16), .in17(x17),
    .in18(x18), .in19(x19), .in20(x20), .in21(x21), .in22(x22), .in23(x23), .in24(x24), .in25(x25),
    .in26(x26), .in27(x27), .in28(x28), .in29(x29), .in30(x30), .in31(x31), .out(ReadData2), .sel(ReadIndex2));

  // Other names for the same wires on the sheet: x1[31:0] = ra; x2[31:0] = sp; x5[31:0] = t0; x6[31:0] = t1;
  //   x7[31:0] = t2; x8[31:0] = s0; x9[31:0] = s1; x10[31:0] = a0

  // Notes on the sheet:
  //   INPUTS to your circuit
  //   DON'T CHANGE THE LOCATIONS OF THE INPUTS AND OUTPUTS!
  //   These are DEBUG/TEST outputs from your circuit.
  //   OUTPUTS from your circuit
endmodule
